# Fritzing sketch fritzing (saved by Fritzing 1.0.3b)
breadboards: 1

parts:
  Part1 = Arduino Uno (Rev3)
  R1 = Resistor [tolerance=±5% power=0.25W resistance=330 package=THT]
  LED1 = LED - 5mm [color="Red (633nm)" current=0.030A package="5 mm [THT]"]
  S1 = Pushbutton [package="[THT]"]
  R2 = Resistor [tolerance=±5% power=0.25W resistance=330 package=THT]

nets:
  N1: Part1.D8, S1.Pin_1, S1.Pin_2, R2.Pin_0
  N2: Part1.D7, LED1.anode
  N3: R1.Pin_0, R2.Pin_1
  N4: R1.Pin_1, LED1.cathode
  N5: S1.Pin_3, S1.Pin_4
